# Fritzing sketch HSG Door Hack v0_5 (saved by Fritzing 0.7.7b)
breadboards: 1

parts:
  Arduino_Ethernet_Shield1 = Arduino Ethernet Shield
  Arduino1 = Arduino  # not connected
  J1 = Infrared Proximity Sensor
  K1 = Relay [part_number=FRS1B-S package=THT]
  LED1 = LED - 3mm [color="Red (633nm)" package="3 mm [THT]"]
  LED2 = LED - 3mm [color="Green (565nm)" package="3 mm [THT]"]
  R1 = Resistor [tolerance=±5% resistance=220 package="0805 [SMD]"]
  R2 = Resistor [tolerance=±5% resistance=220 package="0805 [SMD]"]
  S1 = Pushbutton [package="[THT]"]
  R3 = Resistor [tolerance=±5% resistance=220 package="0805 [SMD]"]

nets:
  N1: Arduino_Ethernet_Shield1.D9, S1.Pin_3, S1.Pin_4, R3.Pin_1
  N2: Arduino_Ethernet_Shield1.D8, LED1.anode
  N3: Arduino_Ethernet_Shield1.D7, LED2.anode
  N4: Arduino_Ethernet_Shield1.D2, K1.C1, K1.C2
  +5V: Arduino_Ethernet_Shield1.+5V, J1.Vcc, S1.Pin_1, S1.Pin_2
  GND: Arduino_Ethernet_Shield1.GND, J1.GND, R1.Pin_0, R2.Pin_0, R3.Pin_0
  N5: Arduino_Ethernet_Shield1.A2, J1.Vout
  N6: LED1.cathode, R1.Pin_1
  N7: LED2.cathode, R2.Pin_1
